// Logisim project Universal_Shift_register.circ as structural Verilog: 5 circuits, main circuit main
module main (
  input  I0,
  input  I1,
  input  I2,
  input  I3,
  input  D,
  input  D1,
  input  [1:0] E,
  input  S,
  input  R,
  output Q,
  output Q1
);

  wire clock_1_out, d_ff_2_q, d_ff_3_q, multiplexer_1_out, multiplexer_2_out, multiplexer_3_out,
       multiplexer_4_out;

  Clock clock_1 (.out(clock_1_out));
  Multiplexer #(.select(2)) multiplexer_1 (
    .in0(D), .in1(d_ff_2_q), .in2(I0), .in3(Q1), .out(multiplexer_1_out), .sel(E));
  D_Flip_Flop d_ff_1 (.D(multiplexer_1_out), .clk(clock_1_out), .Q(Q1), .preset(S), .reset(R));  // open: Qn
  Multiplexer #(.select(2)) multiplexer_2 (
    .in0(Q1), .in1(d_ff_3_q), .in2(I1), .in3(d_ff_2_q), .out(multiplexer_2_out), .sel(E));
  D_Flip_Flop d_ff_2 (.D(multiplexer_2_out), .clk(clock_1_out), .Q(d_ff_2_q), .preset(S), .reset(R));  // open: Qn
  Multiplexer #(.select(2)) multiplexer_3 (
    .in0(d_ff_2_q), .in1(Q), .in2(I2), .in3(d_ff_3_q), .out(multiplexer_3_out), .sel(E));
  D_Flip_Flop d_ff_3 (.D(multiplexer_3_out), .clk(clock_1_out), .Q(d_ff_3_q), .preset(S), .reset(R));  // open: Qn
  Multiplexer #(.select(2)) multiplexer_4 (
    .in0(d_ff_3_q), .in1(D1), .in2(I3), .in3(Q), .out(multiplexer_4_out), .sel(E));
  D_Flip_Flop d_ff_4 (.D(multiplexer_4_out), .clk(clock_1_out), .Q(Q), .preset(S), .reset(R));  // open: Qn
endmodule

module Right_shift_register (
  input  in_1,
  input  in_2,
  input  in_3
);

  wire clock_1_out, d_ff_1_q, d_ff_2_q, d_ff_3_q;

  D_Flip_Flop d_ff_1 (.D(in_2), .clk(clock_1_out), .Q(d_ff_1_q), .preset(in_1), .reset(in_3));  // open: Qn
  Clock clock_1 (.out(clock_1_out));
  D_Flip_Flop d_ff_2 (.D(d_ff_1_q), .clk(clock_1_out), .Q(d_ff_2_q), .preset(in_1), .reset(in_3));  // open: Qn
  D_Flip_Flop d_ff_3 (.D(d_ff_2_q), .clk(clock_1_out), .Q(d_ff_3_q), .preset(in_1), .reset(in_3));  // open: Qn
  D_Flip_Flop d_ff_4 (.D(d_ff_3_q), .clk(clock_1_out), .preset(in_1), .reset(in_3));  // open: Q, Qn
endmodule

module Left_shift_register (
  input  D,
  input  in_2,
  input  in_3,
  output Q
);

  wire clock_1_out, d_ff_2_q, d_ff_3_q, d_ff_4_q;

  D_Flip_Flop d_ff_1 (.D(d_ff_2_q), .clk(clock_1_out), .Q(Q), .preset(in_2), .reset(in_3));  // open: Qn
  Clock clock_1 (.out(clock_1_out));
  D_Flip_Flop d_ff_2 (.D(d_ff_3_q), .clk(clock_1_out), .Q(d_ff_2_q), .preset(in_2), .reset(in_3));  // open: Qn
  D_Flip_Flop d_ff_3 (.D(d_ff_4_q), .clk(clock_1_out), .Q(d_ff_3_q), .preset(in_2), .reset(in_3));  // open: Qn
  D_Flip_Flop d_ff_4 (.D(D), .clk(clock_1_out), .Q(d_ff_4_q), .preset(in_2), .reset(in_3));  // open: Qn
endmodule

module Both_shift_register (
  input  in_1,
  input  in_2,
  input  E,
  input  S,
  input  R,
  output out_6,
  output out_7
);

  wire clock_1_out, d_ff_2_q, d_ff_3_q, multiplexer_1_out, multiplexer_2_out, multiplexer_3_out,
       multiplexer_4_out;

  Clock clock_1 (.out(clock_1_out));
  D_Flip_Flop d_ff_1 (.D(multiplexer_1_out), .clk(clock_1_out), .Q(out_7), .preset(S), .reset(R));  // open: Qn
  Multiplexer multiplexer_1 (.in0(in_1), .in1(d_ff_2_q), .out(multiplexer_1_out), .sel(E));
  Multiplexer multiplexer_2 (.in0(out_7), .in1(d_ff_3_q), .out(multiplexer_2_out), .sel(E));
  D_Flip_Flop d_ff_2 (.D(multiplexer_2_out), .clk(clock_1_out), .Q(d_ff_2_q), .preset(S), .reset(R));  // open: Qn
  Multiplexer multiplexer_3 (.in0(d_ff_2_q), .in1(out_6), .out(multiplexer_3_out), .sel(E));
  D_Flip_Flop d_ff_3 (.D(multiplexer_3_out), .clk(clock_1_out), .Q(d_ff_3_q), .preset(S), .reset(R));  // open: Qn
  Multiplexer multiplexer_4 (.in0(d_ff_3_q), .in1(in_2), .out(multiplexer_4_out), .sel(E));
  D_Flip_Flop d_ff_4 (.D(multiplexer_4_out), .clk(clock_1_out), .Q(out_6), .preset(S), .reset(R));  // open: Qn
endmodule

module Universal_shift_register (
  input  I0,
  input  I1,
  input  I2,
  input  I3,
  input  D,
  input  D1,
  input  [1:0] E,
  input  S,
  input  R,
  output Q,
  output Q1
);

  wire clock_1_out, d_ff_2_q, d_ff_3_q, multiplexer_1_out, multiplexer_2_out, multiplexer_3_out,
       multiplexer_4_out;

  Clock clock_1 (.out(clock_1_out));
  Multiplexer #(.select(2)) multiplexer_1 (
    .in0(D), .in1(d_ff_2_q), .in2(I0), .in3(Q1), .out(multiplexer_1_out), .sel(E));
  D_Flip_Flop d_ff_1 (.D(multiplexer_1_out), .clk(clock_1_out), .Q(Q1), .preset(S), .reset(R));  // open: Qn
  Multiplexer #(.select(2)) multiplexer_2 (
    .in0(Q1), .in1(d_ff_3_q), .in2(I1), .in3(d_ff_2_q), .out(multiplexer_2_out), .sel(E));
  D_Flip_Flop d_ff_2 (.D(multiplexer_2_out), .clk(clock_1_out), .Q(d_ff_2_q), .preset(S), .reset(R));  // open: Qn
  Multiplexer #(.select(2)) multiplexer_3 (
    .in0(d_ff_2_q), .in1(Q), .in2(I2), .in3(d_ff_3_q), .out(multiplexer_3_out), .sel(E));
  D_Flip_Flop d_ff_3 (.D(multiplexer_3_out), .clk(clock_1_out), .Q(d_ff_3_q), .preset(S), .reset(R));  // open: Qn
  Multiplexer #(.select(2)) multiplexer_4 (
    .in0(d_ff_3_q), .in1(D1), .in2(I3), .in3(Q), .out(multiplexer_4_out), .sel(E));
  D_Flip_Flop d_ff_4 (.D(multiplexer_4_out), .clk(clock_1_out), .Q(Q), .preset(S), .reset(R));  // open: Qn
endmodule
